// Digital circuit rjstack.dig as structural Verilog
module rjstack (
  input  clk,
  input  [2:0] i,
  input  push,
  input  pop,
  input  we_itos,
  input  we_nostos,
  input  we_ytos,
  input  store,
  output [15:0] ros,
  output [15:0] tos,
  output [11:0] sp,
  output [15:0] nos,
  output [15:0] y,
  output [2:0] i_2
);

  wire [2:0] pc_out;
  wire [4:0] program_d;

  Counter #(.Bits(3)) pc (.en(1'b1), .C(clk), .clr(1'b0), .out(pc_out));  // open: ovf
  EEPROMDualPort #(.AddrBits(3), .Bits(8)) \program  (
    .A(pc_out), .Din({i, we_ytos, we_nostos, we_itos, pop, push}), .str(store), .C(clk), .ld(1'b1),
    .D({i_2, program_d}));
  LED u_push (.in(program_d[0]));
  LED u_pop (.in(program_d[1]));
  LED i__gt_tos (.in(program_d[2]));
  LED nos__gt_tos (.in(program_d[3]));
  LED y__gt_tos (.in(program_d[4]));
  stack stack_1 (
    .clk(clk), .push(program_d[0]), .pop(program_d[1]), .we_itos(program_d[2]), .we_nostos(program_d[3]),
    .we_ytos(program_d[4]), .i({{13{1'b0}}, i_2}), .y(y), .sp(sp), .ros(ros), .nos(nos), .tos(tos));
  Add #(.Bits(16)) alu (.a(nos), .b(tos), .c_i(1'b0), .s(y));  // open: c_o

  // Other names for the same wires on the sheet: c = clk

  // Notes on the sheet:
  //   [01]
  //   FPGA Stack Machine CPU from Scratch
  //   Running the First Program
  //   rj45Creates
  //   contents of program (hex, n*v repeats v):
  //   24,45,12,85,12
endmodule
